# Fritzing sketch Arduino_Nano_DSO_BT_simple (saved by Fritzing 0.9.3b)
breadboards: 1

parts:
  Nano = Arduino Nano (Rev3.0)
  C2 = Ceramic Capacitor [capacitance=100nF voltage=0.1kV package="100 mil [THT, multilayer]"]
  R3 = Resistor [tolerance=±1% resistance=100k package=THT]
  D2 = Rectifier Diode [part_number="BAT 42" package="300 mil [THT]"]
  HC-05 = Bluetooth HC-05
  R4 = Resistor [tolerance=±1% resistance=10k package=THT]
  R6 = Resistor [tolerance=±1% resistance=100k package=THT]
  R5 = Resistor [tolerance=±1% resistance=6.8M package=THT]
  C3 = Ceramic Capacitor [capacitance=100nF voltage=0.1kV package="100 mil [THT, multilayer]"]
  R7 = Resistor [tolerance=±1% resistance=2.2k package=THT]

nets:
  N1: Nano.D1/TX, HC-05.RXD
  N2: Nano.D0/RX, D2.anode
  GND: Nano.GND, HC-05.GND, R6.Pin_1, C3.1
  N3: Nano.D10, R7.Pin_0
  5V: Nano.5V, HC-05.VCC
  N4: Nano.A5, R3.Pin_1, R6.Pin_0, R5.Pin_1
  N5: Nano.A0, R4.Pin_1
  N6: Nano.AREF, R3.Pin_0
  N7: C2.0, R4.Pin_0, R5.Pin_0
  N8: D2.cathode, HC-05.TXD
  N9: C3.0, R7.Pin_1
