# Fritzing sketch Arduino_Nano_DSO_simple (saved by Fritzing 0.9.3b)
breadboards: 1

parts:
  R8 = Resistor [tolerance=±1% resistance=6.8M package=THT]
  Nano1 = Arduino Nano (Rev3.0)
  C4 = Ceramic Capacitor [capacitance=100nF voltage=0.1kV package="100 mil [THT, multilayer]"]
  R9 = Resistor [tolerance=±1% resistance=100k package=THT]
  R10 = Resistor [tolerance=±1% resistance=100k package=THT]
  R11 = Resistor [tolerance=±1% resistance=10k package=THT]
  C5 = Ceramic Capacitor [capacitance=100nF voltage=0.1kV package="100 mil [THT, multilayer]"]
  R12 = Resistor [tolerance=±1% resistance=2.2k package=THT]

nets:
  N1: R8.Pin_0, C4.0, R11.Pin_0
  N2: R8.Pin_1, Nano1.A5, R9.Pin_0, R10.Pin_1
  N3: Nano1.GND, C5.1
  N4: Nano1.D10, R12.Pin_0
  5V: Nano1.5V
  N5: Nano1.A0, R11.Pin_1
  N6: Nano1.AREF, R10.Pin_0
  GND: R9.Pin_1
  N7: C5.0, R12.Pin_1
