# Fritzing sketch Arduino_Nano_DSO (saved by Fritzing 0.9.3b)
breadboards: 1

parts:
  Nano = Arduino Nano (Rev3.0)
  C1 = Ceramic Capacitor [capacitance=100nF voltage=0.1kV package="100 mil [THT, multilayer]"]
  C2 = Ceramic Capacitor [capacitance=100nF voltage=0.1kV package="100 mil [THT, multilayer]"]
  C3 = Ceramic Capacitor [capacitance=100nF voltage=0.1kV package="100 mil [THT, multilayer]"]
  R1 = Resistor [tolerance=±1% resistance=1M package=THT]
  R2 = Resistor [tolerance=±1% resistance=1M package=THT]
  R3 = Resistor [tolerance=±1% resistance=10k package=THT]
  R4 = Resistor [tolerance=±1% resistance=1M package=THT]
  R5 = Resistor [tolerance=±1% resistance=100k package=THT]
  R6 = Resistor [tolerance=±5% resistance=220k package=THT]
  R7 = Resistor [tolerance=±5% resistance=220k package=THT]
  R8 = Resistor [tolerance=±1% resistance=100k package=THT]
  R9 = Resistor [tolerance=±1% resistance=100k package=THT]
  C4 = Tantalum Capacitor [capacitance=22µF package="100 mil [THT, tantalum]"]
  AC/DC_Switch_2x = Toggle Switch [package=THT]
  S1 = Toggle Switch [package=THT]
  R10 = Resistor [tolerance=±1% resistance=10k package=THT]
  D2 = Rectifier Diode [part_number="BAT 42" package="300 mil [THT]"]
  HC-05 = Bluetooth HC-05

nets:
  N1: Nano.D1/TX, HC-05.RXD
  N2: Nano.D0/RX, D2.anode
  GND: Nano.GND, Nano.D8, R9.Pin_1, C4.-, AC/DC_Switch_2x.L2, S1.COM, HC-05.GND
  N3: Nano.D2, R5.Pin_1
  N4: Nano.D3, S1.L1
  5V: Nano.5V, HC-05.VCC
  N5: Nano.A2, R2.Pin_1, R10.Pin_0
  N6: Nano.A1, R1.Pin_1, R6.Pin_0, R7.Pin_0
  N7: Nano.A0, R3.Pin_0, R4.Pin_0
  N8: Nano.AREF, R8.Pin_1
  N9: C1.0, R3.Pin_1
  N10: C2.0, R1.Pin_0
  N11: C3.0, R2.Pin_0
  N12: R4.Pin_1, R6.Pin_1, R7.Pin_1, AC/DC_Switch_2x.COM, R10.Pin_1
  N13: R8.Pin_0, R9.Pin_0, C4.+, AC/DC_Switch_2x.L1
  N14: D2.cathode, HC-05.TXD

notes:
  >4 MOhm
  coupled
