# Fritzing sketch Arduino_Nano_DSO_BT (saved by Fritzing 0.9.3b)
circuit board: 8.46667cm x 5.64444cm
breadboards: 1

parts:
  Nano = Arduino Nano (Rev3.0)
  C1 = Ceramic Capacitor [capacitance=100nF voltage=0.1kV package="100 mil [THT, multilayer]"]
  C2 = Ceramic Capacitor [capacitance=100nF voltage=0.1kV package="100 mil [THT, multilayer]"]
  C3 = Ceramic Capacitor [capacitance=100nF voltage=0.1kV package="100 mil [THT, multilayer]"]
  R1 = Resistor [tolerance=±1% resistance=1M package=THT]
  R2 = Resistor [tolerance=±1% resistance=1M package=THT]
  R3 = Resistor [tolerance=±1% resistance=10k package=THT]
  R4 = Resistor [tolerance=±1% resistance=1M package=THT]
  R5 = Resistor [tolerance=±1% resistance=100k package=THT]
  R6 = Resistor [tolerance=±5% resistance=220k package=THT]
  R7 = Resistor [tolerance=±5% resistance=220k package=THT]
  R9 = Resistor [tolerance=±1% resistance=100k package=THT]
  C4 = Tantalum Capacitor [capacitance=6.8µF package="100 mil [THT, tantalum]"]
  R10 = Resistor [tolerance=±1% resistance=10k package=THT]
  D2 = Rectifier Diode [part_number="BAT 42" package="300 mil [THT]"]
  HC-05 = Bluetooth HC-05
  C5 = Ceramic Capacitor [capacitance=100nF voltage=0.1kV package="100 mil [THT, multilayer]"]
  R11 = Resistor [tolerance=±1% resistance=2.2k package=THT]
  R12 = Resistor [tolerance=±1% resistance=100k package=THT]

nets:
  N1: Nano.D1/TX, HC-05.RXD
  N2: Nano.D0/RX, D2.anode
  GND: Nano.GND, Nano.D8, R9.Pin_1, C4.-, HC-05.GND, C5.0
  N3: Nano.D2, R5.Pin_1
  N4: Nano.D10, R11.Pin_1
  5V: Nano.5V, HC-05.VCC
  N5: Nano.A5, R4.Pin_1, R6.Pin_1, R7.Pin_1, R9.Pin_0, C4.+, R10.Pin_1, R12.Pin_1
  N6: Nano.A2, R2.Pin_1, R10.Pin_0
  N7: Nano.A1, R1.Pin_1, R6.Pin_0, R7.Pin_0
  N8: Nano.A0, R3.Pin_0, R4.Pin_0
  N9: Nano.AREF, R12.Pin_0
  N10: C1.0, R3.Pin_1
  N11: C2.0, R1.Pin_0
  N12: C3.0, R2.Pin_0
  N13: D2.cathode, HC-05.TXD
  N14: C5.1, R11.Pin_0

notes:
  >4.7 MOhm
  <-Sine/Triangle/Sawtooth
  >4 MOhm
  <-0.1 - 8 MHz Sqare wave
  1.1V / VCC DC  AC
  11V DC  AC
  110V DC  AC
  <-External trigger input
  BlueDisplay / DSO, 2.0
