# Fritzing sketch Arduino_Nano_DSO_Simple (saved by Fritzing 0.9.3b)
breadboards: 1

parts:
  Nano = Arduino Nano (Rev3.0)
  C2 = Ceramic Capacitor [capacitance=100nF voltage=0.1kV package="100 mil [THT, multilayer]"]
  R3 = Resistor [tolerance=±1% resistance=2M package=THT]
  D2 = Rectifier Diode [part_number="BAT 42" package="300 mil [THT]"]
  HC-05 = Bluetooth HC-05
  part = Resistor [tolerance=±1% resistance=2M package=THT]
  R4 = Resistor [tolerance=±1% resistance=10k package=THT]
  R5 = Resistor [tolerance=±1% resistance=10k package=THT]

nets:
  N1: Nano.D1/TX, HC-05.RXD
  N2: Nano.D0/RX, D2.anode
  GND: Nano.GND, R3.Pin_1, HC-05.GND
  5V: Nano.5V, HC-05.VCC
  N3: Nano.A1, R3.Pin_0, part.Pin_1, R4.Pin_1
  N4: Nano.A0, R5.Pin_1
  N5: Nano.AREF, part.Pin_0
  N6: C2.0, R4.Pin_0
  N7: D2.cathode, HC-05.TXD
